# Fritzing sketch Circuit_Layout (saved by Fritzing 0.9.3b)

parts:
  Part1 = Arduino Ethernet Shield (Rev3)
  Part2 = Arduino Uno (Rev3) - ICSP  # not connected
  U1 = POT [package=pot_mammoth]
  Part3 = InvenSense MPU6050
  M2 = ESC
  920KV_Motor2 = DJI 920 KV Motor
  U2 = LIPO-1000mAh [package=lipo-1000]
  LED3 = smd LED [color="Green (565nm)" package="0603 [SMD]"]
  LED2 = smd LED [color="White (4500K)" package="0603 [SMD]"]
  LED1 = smd LED [color="Blue (470nm)" package="0603 [SMD]"]

nets:
  N1: Part1.PWM_D9, M2.DATA
  GND: Part1.GND, U1.S, Part3.GND, U2.-, LED2.cathode
  N2: Part1.A0, U1.A
  N3: Part1.A4/SDA, Part3.SDA
  N4: Part1.A5/SCL, Part3.SCL
  N5: Part1.PWM_D5, LED3.anode
  N6: Part1.PWM_D6, LED2.anode
  N7: Part1.D7, LED1.anode
  5V: Part1.5V, U1.E, Part3.VCC
  N8: M2.U, 920KV_Motor2.u
  N9: M2.V, 920KV_Motor2.v
  N10: M2.W, 920KV_Motor2.w

notes:
  + and - are INTENTIONALLY left disconnected. ----->
  Arduino UNO w/ ethernet shield
  3S Lipo Battery

custom parts:
  DJI 920 KV Motor: DJI Brushless Outrunner 2212/920K Motor F330-550

// code stored in the sketch: MecE668.ino

